# Fritzing sketch Teclado (saved by Fritzing 0.9.6b)
circuit board: 16cm x 8.5cm
breadboards: 6

parts:
  S1 = Pushbutton [package="[THT]"]
  S2 = Pushbutton [package="[THT]"]
  S3 = Pushbutton [package="[THT]"]
  S4 = Pushbutton [package="[THT]"]
  S5 = Pushbutton [package="[THT]"]
  S6 = Pushbutton [package="[THT]"]
  S7 = Pushbutton [package="[THT]"]
  S8 = Pushbutton [package="[THT]"]
  S9 = Pushbutton [package="[THT]"]
  S10 = Pushbutton [package="[THT]"]
  S11 = Pushbutton [package="[THT]"]
  S12 = Pushbutton [package="[THT]"]
  S13 = Pushbutton [package="[THT]"]
  S14 = Pushbutton [package="[THT]"]
  S15 = Pushbutton [package="[THT]"]
  S16 = Pushbutton [package="[THT]"]
  S17 = Pushbutton [package="[THT]"]
  S18 = Pushbutton [package="[THT]"]
  S19 = Pushbutton [package="[THT]"]
  S20 = Pushbutton [package="[THT]"]
  S21 = Pushbutton [package="[THT]"]
  S22 = Pushbutton [package="[THT]"]
  S23 = Pushbutton [package="[THT]"]
  S24 = Pushbutton [package="[THT]"]
  S25 = Pushbutton [package="[THT]"]
  S26 = Pushbutton [package="[THT]"]
  S27 = Pushbutton [package="[THT]"]
  S28 = Pushbutton [package="[THT]"]
  S29 = Pushbutton [package="[THT]"]
  S30 = Pushbutton [package="[THT]"]
  S31 = Pushbutton [package="[THT]"]
  S32 = Pushbutton [package="[THT]"]
  S33 = Pushbutton [package="[THT]"]
  S34 = Pushbutton [package="[THT]"]
  S35 = Pushbutton [package="[THT]"]
  S36 = Pushbutton [package="[THT]"]
  S37 = Pushbutton [package="[THT]"]
  S38 = Pushbutton [package="[THT]"]
  S39 = Pushbutton [package="[THT]"]
  S40 = Pushbutton [package="[THT]"]
  S41 = Pushbutton [package="[THT]"]
  S42 = Pushbutton [package="[THT]"]
  S43 = Pushbutton [package="[THT]"]
  S44 = Pushbutton [package="[THT]"]
  S45 = Pushbutton [package="[THT]"]
  S46 = Pushbutton [package="[THT]"]
  S47 = Pushbutton [package="[THT]"]
  S48 = Pushbutton [package="[THT]"]
  D1 = Diode [package=diode-hv]
  D2 = Diode [package=diode-hv]
  D3 = Diode [package=diode-hv]
  D4 = Diode [package=diode-hv]
  D5 = Diode [package=diode-hv]
  D6 = Diode [package=diode-hv]
  D7 = Diode [package=diode-hv]
  D8 = Diode [package=diode-hv]
  D9 = Diode [package=diode-hv]
  D10 = Diode [package=diode-hv]
  D11 = Diode [package=diode-hv]
  D12 = Diode [package=diode-hv]
  Screen = OLED 0.96" 128x64 I2C SSD1306
  Nano = Arduino Nano (Rev3.0)

nets:
  N1: S1.Pin_1, S1.Pin_2, S13.Pin_1, S13.Pin_2, S25.Pin_1, S25.Pin_2, S37.Pin_1, S37.Pin_2, D1.A
  N2: S1.Pin_3, S1.Pin_4, S2.Pin_3, S2.Pin_4, S3.Pin_3, S3.Pin_4, S4.Pin_3, S4.Pin_4, S5.Pin_3, S5.Pin_4, S6.Pin_3, S6.Pin_4, S7.Pin_3, S7.Pin_4, S8.Pin_3, S8.Pin_4, S9.Pin_3, S9.Pin_4, S10.Pin_3, S10.Pin_4, S11.Pin_3, S11.Pin_4, S12.Pin_3, S12.Pin_4, Nano.A1
  N3: S2.Pin_1, S2.Pin_2, S14.Pin_1, S14.Pin_2, S26.Pin_1, S26.Pin_2, S38.Pin_1, S38.Pin_2, D2.A
  N4: S3.Pin_1, S3.Pin_2, S15.Pin_1, S15.Pin_2, S27.Pin_1, S27.Pin_2, S39.Pin_1, S39.Pin_2, D3.A
  N5: S4.Pin_1, S4.Pin_2, S16.Pin_1, S16.Pin_2, S28.Pin_1, S28.Pin_2, S40.Pin_1, S40.Pin_2, D4.A
  N6: S5.Pin_1, S5.Pin_2, S17.Pin_1, S17.Pin_2, S29.Pin_1, S29.Pin_2, S41.Pin_1, S41.Pin_2, D5.A
  N7: S6.Pin_1, S6.Pin_2, S18.Pin_1, S18.Pin_2, S30.Pin_1, S30.Pin_2, S42.Pin_1, S42.Pin_2, D6.A
  N8: S7.Pin_1, S7.Pin_2, S19.Pin_1, S19.Pin_2, S31.Pin_1, S31.Pin_2, S43.Pin_1, S43.Pin_2, D7.A
  N9: S8.Pin_1, S8.Pin_2, S20.Pin_1, S20.Pin_2, S32.Pin_1, S32.Pin_2, S44.Pin_1, S44.Pin_2, D8.A
  N10: S9.Pin_1, S9.Pin_2, S21.Pin_1, S21.Pin_2, S33.Pin_1, S33.Pin_2, S45.Pin_1, S45.Pin_2, D9.A
  N11: S10.Pin_1, S10.Pin_2, S22.Pin_1, S22.Pin_2, S34.Pin_1, S34.Pin_2, S46.Pin_1, S46.Pin_2, D10.A
  N12: S11.Pin_1, S11.Pin_2, S23.Pin_1, S23.Pin_2, S35.Pin_1, S35.Pin_2, S47.Pin_1, S47.Pin_2, D11.A
  N13: S12.Pin_1, S12.Pin_2, S24.Pin_1, S24.Pin_2, S36.Pin_1, S36.Pin_2, S48.Pin_1, S48.Pin_2, D12.A
  N14: S13.Pin_3, S13.Pin_4, S14.Pin_3, S14.Pin_4, S15.Pin_3, S15.Pin_4, S16.Pin_3, S16.Pin_4, S17.Pin_3, S17.Pin_4, S18.Pin_3, S18.Pin_4, S19.Pin_3, S19.Pin_4, S20.Pin_3, S20.Pin_4, S21.Pin_3, S21.Pin_4, S22.Pin_3, S22.Pin_4, S23.Pin_3, S23.Pin_4, S24.Pin_3, S24.Pin_4, Nano.A2
  N15: S25.Pin_3, S25.Pin_4, S26.Pin_3, S26.Pin_4, S27.Pin_3, S27.Pin_4, S28.Pin_3, S28.Pin_4, S29.Pin_3, S29.Pin_4, S30.Pin_3, S30.Pin_4, S31.Pin_3, S31.Pin_4, S32.Pin_3, S32.Pin_4, S33.Pin_3, S33.Pin_4, S34.Pin_3, S34.Pin_4, S35.Pin_3, S35.Pin_4, S36.Pin_3, S36.Pin_4, Nano.A3
  N16: S37.Pin_3, S37.Pin_4, S38.Pin_3, S38.Pin_4, S39.Pin_3, S39.Pin_4, S40.Pin_3, S40.Pin_4, S41.Pin_3, S41.Pin_4, S42.Pin_3, S42.Pin_4, S43.Pin_3, S43.Pin_4, S44.Pin_3, S44.Pin_4, S45.Pin_3, S45.Pin_4, S46.Pin_3, S46.Pin_4, S47.Pin_3, S47.Pin_4, S48.Pin_3, S48.Pin_4, Nano.A6
  N17: D1.C, Nano.D2
  N18: D2.C, Nano.D3
  N19: D3.C, Nano.D4
  N20: D4.C, Nano.D5
  N21: D5.C, Nano.D6
  N22: D6.C, Nano.D7
  N23: D7.C, Nano.D8
  N24: D8.C, Nano.D9
  N25: D9.C, Nano.D10
  N26: D10.C, Nano.D11/MOSI
  N27: D11.C, Nano.D12/MISO
  N28: D12.C, Nano.A7
  VCC: Screen.VCC, Nano.5V
  GND: Screen.GND, Nano.GND
  N29: Screen.SCL, Nano.A5
  N30: Screen.SCA, Nano.A4
